# Fritzing sketch HybridKeyboard (saved by Fritzing 0.8.7b)
breadboards: 1

parts:
  Teensy1 = Teensy 2.0 BreadBoard Pins only
  D1 = Rectifier Diode [part_number=1N4001 package="300 mil [THT]"]
  R4 = 10k ohm Resistor [package="2010 [SMD]"]
  R3 = 10k ohm Resistor [package="2010 [SMD]"]
  R2 = 10k ohm Resistor [package="2010 [SMD]"]
  R1 = 10k ohm Resistor [package="2010 [SMD]"]
  R5 = 10k ohm Resistor [package="2010 [SMD]"]
  R6 = 10k ohm Resistor [package="2010 [SMD]"]
  74HC_1 = 74HC 4514 [package="DIP24 [THT]"]
  R7 = 1k ohm Resistor [package="2010 [SMD]"]
  R8 = 1k ohm Resistor [package="2010 [SMD]"]
  Adafruit_Bluefruit_HID1 = Adafruit Bluefruit EZ-Key Breadboard Pins Only Small Schematic
  BAT2 = Battery Holders [package=battery-aa]
  BAT3 = Battery Holders [package=battery-aa]
  LED1 = LED - 3mm [color="Green (565nm)" package="3 mm [THT]"]
  LED2 = LED - 3mm [color="Green (565nm)" package="3 mm [THT]"]
  BAT1 = Battery Holders [package=battery-aa]
  74HC1 = 74HC251 [package="DIP16 [THT]"]
  D2 = Rectifier Diode [part_number=1N4001 package="300 mil [THT]"]

nets:
  GND: Teensy1.GND, R4.Pin_1, R3.Pin_1, R2.Pin_1, R1.Pin_1, R5.Pin_0, R6.Pin_0, 74HC_1.12_GND, 74HC_1.23_/E, R7.Pin_0, Adafruit_Bluefruit_HID1.G, BAT3.+, 74HC1./OE, 74HC1.GND
  N1: Teensy1.B0, 74HC_1.2_A0
  N2: Teensy1.B1, 74HC_1.3_A1
  N3: Teensy1.B2, 74HC_1.21_A2
  N4: Teensy1.B3, 74HC_1.22_A3
  N5: Teensy1.B7, 74HC1.Y
  N6: Teensy1.D2, Adafruit_Bluefruit_HID1.TX
  N7: Teensy1.D3, Adafruit_Bluefruit_HID1.RX
  N8: Teensy1.D6, LED2.anode
  N9: Teensy1.D7, LED1.cathode
  N10: Teensy1.B4, 74HC1.S0
  N11: Teensy1.B5, 74HC1.S1
  N12: Teensy1.B6, 74HC1.S2
  N13: Teensy1.F7, Adafruit_Bluefruit_HID1.PB
  N14: Teensy1.F6, Adafruit_Bluefruit_HID1.RS
  VCC: Teensy1.VCC, 74HC_1.1_LE, 74HC_1.24_Vcc, R8.Pin_0, Adafruit_Bluefruit_HID1.3v, 74HC1.Vcc
  N15: D1.cathode, Adafruit_Bluefruit_HID1.Vin, D2.cathode
  Teensy VBUS: D1.anode
  Row 3: R4.Pin_0, 74HC1.I3
  Row 2: R3.Pin_0, 74HC1.I2
  Row 1: R2.Pin_0, 74HC1.I1
  Row 0: R1.Pin_0, 74HC1.I0
  Row 4: R5.Pin_1, 74HC1.I4
  Row 5: R6.Pin_1, 74HC1.I5
  Column 7: 74HC_1.4_Q7
  Column 6: 74HC_1.5_Q6
  Column 5: 74HC_1.6_Q5
  Column 4: 74HC_1.7_Q4
  Column 3: 74HC_1.8_Q3
  Column 1: 74HC_1.9_Q1
  Column 2: 74HC_1.10_Q2
  Column 0: 74HC_1.11_Q0
  Column 13: 74HC_1.13_Q13
  Column 12: 74HC_1.14_Q12
  Column 15: 74HC_1.15_Q15
  Column 14: 74HC_1.16_Q14
  Column 9: 74HC_1.17_Q9
  Column 8: 74HC_1.18_Q8
  Column 11: 74HC_1.19_Q11
  Column 10: 74HC_1.20_Q10
  N16: R7.Pin_1, LED2.cathode
  N17: R8.Pin_1, LED1.anode
  N18: BAT2.-, BAT1.+
  N19: BAT2.+, BAT3.-
  N20: BAT1.-, D2.anode

notes:
  +5V Rail
  +3.3V Rail
  Blue=Matrix Control
  Orange = Serial Comm
  Ochre = Bluetooth Control
  Red = Power
  Green = Ground
  Yellow = LEDs
  HybridKeyboard, Joseph 'Tranquilite' Schurig, 1

custom parts:
  Teensy 2.0 BreadBoard Pins only: The Teensy is a complete USB-based microcontoller development system, in a very small footprint, capable of implementing many types of projects. All programming is done via the USB port. No special programmer is needed, only a standard "Mini-B" USB cable and a PC or Macintosh with a USB port.
  10k ohm Resistor: Resistor Basic schematic elements and footprints for 0603, 1206, and PTH resistors.
  74HC 4514: 4-to-16 line decoder/demultiplexer with input latches
  1k ohm Resistor: Resistor Basic schematic elements and footprints for 0603, 1206, and PTH resistors.
  Adafruit Bluefruit EZ-Key Breadboard Pins Only Small Schematic: Adafruit Bluefruit Bluetooth Module
  74HC251: 8-input multiplexer; 3-state
